# Fritzing sketch Fritzing scheme (saved by Fritzing 0.9.1b)
circuit board: 5.64444cm x 8.46667cm
breadboards: 1

parts:
  Arduino_Nano = Arduino Nano (Rev3.0)
  R1 = Resistor [tolerance=±5% resistance=470 package=THT]
  R2 = Resistor [tolerance=±5% resistance=470 package=THT]
  R3 = Resistor [tolerance=±5% resistance=470 package=THT]
  R4 = Resistor [tolerance=±5% resistance=470 package=THT]
  R5 = Resistor [tolerance=±5% resistance=470 package=THT]
  R8 = Resistor [tolerance=±5% resistance=470 package=THT]
  R7 = Resistor [tolerance=±5% resistance=470 package=THT]
  R6 = Resistor [tolerance=±5% resistance=470 package=THT]
  Right_Switch = Pushbutton [package="[THT]"]
  Left_Switch = Pushbutton [package="[THT]"]
  R9 = Resistor [tolerance=±5% resistance=1k package=THT]
  SPKR1 = Loudspeaker
  8x8_LED_Matrix = 8x8 LED Matrix 1388ASR
  R10 = Resistor [tolerance=±5% resistance=1k package=THT]

nets:
  N1: Arduino_Nano.GND, R9.Pin_0, SPKR1.pin2, R10.Pin_0
  N2: Arduino_Nano.D2, R3.Pin_1
  N3: Arduino_Nano.D3, R5.Pin_1
  N4: Arduino_Nano.D4, 8x8_LED_Matrix.Pin_3
  N5: Arduino_Nano.D5, 8x8_LED_Matrix.Pin_4
  N6: Arduino_Nano.D6, R4.Pin_1
  N7: Arduino_Nano.D7, 8x8_LED_Matrix.Pin_6
  N8: Arduino_Nano.D8, R2.Pin_1
  N9: Arduino_Nano.D9, R1.Pin_1
  N10: Arduino_Nano.D10, 8x8_LED_Matrix.Pin_13
  N11: Arduino_Nano.D11/MOSI, 8x8_LED_Matrix.Pin_11
  N12: Arduino_Nano.D12/MISO, 8x8_LED_Matrix.Pin_7#10
  N13: Arduino_Nano.5V, Arduino_Nano.A7, Arduino_Nano.A6, Right_Switch.Pin_1, Right_Switch.Pin_2, Right_Switch.Pin_3, Right_Switch.Pin_4, Left_Switch.Pin_1, Left_Switch.Pin_2, Left_Switch.Pin_3, Left_Switch.Pin_4, R9.Pin_1, R10.Pin_1
  N14: Arduino_Nano.A5, R8.Pin_1
  N15: Arduino_Nano.A3, R7.Pin_1
  N16: Arduino_Nano.A2, SPKR1.pin1
  N17: Arduino_Nano.A1, 8x8_LED_Matrix.Pin_16
  N18: Arduino_Nano.A0, R6.Pin_1
  N19: Arduino_Nano.D13/SCK, 8x8_LED_Matrix.Pin_15
  N20: R1.Pin_0, 8x8_LED_Matrix.Pin_8
  N21: R2.Pin_0, 8x8_LED_Matrix.Pin_7#7
  N22: R3.Pin_0, 8x8_LED_Matrix.Pin_1
  N23: R4.Pin_0, 8x8_LED_Matrix.Pin_5
  N24: R8.Pin_0, 8x8_LED_Matrix.Pin14
  N25: R7.Pin_0, 8x8_LED_Matrix.Pin_12
  N26: R6.Pin_0, 8x8_LED_Matrix.Pin_9

custom parts:
  8x8 LED Matrix 1388ASR: Red Color Common Anode 8x8 LED Matrix
